# Fritzing sketch Schematic (saved by Fritzing 1.0.2b)
breadboards: 1

parts:
  U1 = Adafruit Feather M0 Adalogger [part_number="Adafruit #2796"]
  U2 = Adafruit 128x64 OLED FeatherWing [part_number="Adafruit #4650"]
  U3 = Adafruit FeatherWing Proto [part_number="Adafruit #2884"]
  Q1 = LTR-301 [mpn=1540031NC6090 mn="Würth Elektronik" package=ltr-301]
  LED1 = LEDs [mpn=IR333-A package=led10mm]
  LED2 = LEDs [mpn=XLUR12D mn=SunLED package=led10mm]
  Q3 = LTR-301 [mpn=BPW85B mn="Vishay Semiconductor Opto Division" package=ltr-301]
  Q2 = LTR-301 [mpn=1540031NC6090 mn="Würth Elektronik" package=ltr-301]
  Q4 = LTR-301 [mpn=BPW85B mn="Vishay Semiconductor Opto Division" package=ltr-301]
  R11 = Resistor [tolerance=±5% power=0.25W resistance=47 package=THT]
  R12 = Resistor [tolerance=±5% power=0.25W resistance=100 package=THT]
  R13 = Resistor [tolerance=±5% power=0.25W resistance=300k package=THT]
  R14 = Resistor [tolerance=±5% power=0.25W resistance=10M package=THT]

nets:
  GND: U1.GND, U2.GND, U3.GND, LED1.C, LED2.C, R13.Pin_1, R14.Pin_1
  N1: U1.A4, U3.E
  N2: U1.A3, U3.D
  N3: U1.A2, U3.C, Q1.E, R13.Pin_0
  N4: U1.A1, U3.B
  +3V3: U1.+3V3, U2.3.3V, U3.3V, Q1.C, Q3.C, Q2.C, Q4.C
  N5: U1.!RESET, U2.!RESET
  N6: U1.D12, U3.M, R12.Pin_0
  N7: U1.D11, U3.L, R11.Pin_0
  N8: U1.D9, U2.J
  N9: U1.D6, U2.I
  N10: U1.D5, U2.H
  N11: U1.SCL, U2.SCL
  N12: U1.SDA, U2.SDA
  N13: LED1.A, R12.Pin_1
  N14: LED2.A, R11.Pin_1
  N15: Q2.E, R14.Pin_0

notes:
  Work In Progress, not all values yet determined
  Reflective
  TBD for visible...
  Transmissive

custom parts:
  Adafruit Feather M0 Adalogger: This is the Adafruit Feather M0 Adalogger - our take on an 'all-in-one' Cortex M0 datalogger (or data-reader) with built in USB and battery charging. Its an Adafruit Feather M0 with a microSD holder ready to rock! We have other boards in the Feather family, check'em out here At the Feather M0's heart is an ATSAMD21G18 ARM Cortex M0 processor, clocked at 48 MHz and at 3.3V logic, the same one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
  Adafruit 128x64 OLED FeatherWing: A Feather board without ambition is a Feather board without FeatherWings! This is the FeatherWing 128x64 OLED: it adds a gorgeous 128x64 monochrome OLED plus 3 user buttons to any Feather main board. Using our Feather Stacking Headers or Feather Female Headers you can connect a FeatherWing on top of your Feather board and let the board take flight! These displays are small, only about 1.3"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
  Adafruit FeatherWing Proto: This is the FeatherWing Proto - a prototyping add-on for all Feather boards. Using our Feather Stacking Headers or Feather Female Headers you can connect a FeatherWing on top or bottom of your Feather board and let the board take flight! This has a duplicate breakout for each pin on a Feather, as well as a bunch of plain grid proto holes. For GND and 3.3V, we give you a strip of connected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
